// Logisim project alu.circ as structural Verilog
module L_16_bit_ADD (
  input  [15:0] A,
  input  [15:0] B,
  input  in_3,
  output [15:0] S,
  output C,
  output Gm,
  output Pm
);

  wire four_bit_paralled_adder_1_gm, four_bit_paralled_adder_1_pm, four_bit_paralled_adder_2_gm,
       four_bit_paralled_adder_2_pm, four_bit_paralled_adder_3_gm, four_bit_paralled_adder_3_pm,
       four_bit_paralled_adder_4_gm, four_bit_paralled_adder_4_pm, four_bit_parallel_carry_1_c1,
       four_bit_parallel_carry_1_c2, four_bit_parallel_carry_1_c3;

  // Probe on A
  // Probe on B
  four_bit_paralled_adder four_bit_paralled_adder_1 (
    .A(A[3:0]), .B(B[3:0]), .S(S[3:0]), .Pm(four_bit_paralled_adder_1_pm), .Gm(four_bit_paralled_adder_1_gm));  // open: Cin, C
  four_bit_paralled_adder four_bit_paralled_adder_2 (
    .A(A[7:4]), .B(B[7:4]), .Cin(four_bit_parallel_carry_1_c1), .S(S[7:4]),
    .Pm(four_bit_paralled_adder_2_pm), .Gm(four_bit_paralled_adder_2_gm));  // open: C
  four_bit_paralled_adder four_bit_paralled_adder_3 (
    .A(A[11:8]), .B(B[11:8]), .Cin(four_bit_parallel_carry_1_c2), .S(S[11:8]),
    .Pm(four_bit_paralled_adder_3_pm), .Gm(four_bit_paralled_adder_3_gm));  // open: C
  four_bit_paralled_adder four_bit_paralled_adder_4 (
    .A(A[15:12]), .B(B[15:12]), .Cin(four_bit_parallel_carry_1_c3), .S(S[15:12]),
    .Pm(four_bit_paralled_adder_4_pm), .Gm(four_bit_paralled_adder_4_gm));  // open: C
  // Probe on S
  four_bit_parallel_carry four_bit_parallel_carry_1 (
    .G0(four_bit_paralled_adder_1_gm), .P0(four_bit_paralled_adder_1_pm), .G1(four_bit_paralled_adder_2_gm),
    .P1(four_bit_paralled_adder_2_pm), .G2(four_bit_paralled_adder_3_gm), .P2(four_bit_paralled_adder_3_pm),
    .G3(four_bit_paralled_adder_4_gm), .P3(four_bit_paralled_adder_4_pm), .Cin(in_3),
    .C1(four_bit_parallel_carry_1_c1), .C2(four_bit_parallel_carry_1_c2), .C3(four_bit_parallel_carry_1_c3),
    .C4(C), .Gm(Gm), .Pm(Pm));
endmodule

module L_16_bit_SUB (
  input  [15:0] in_1,
  input  [15:0] in_2,
  input  in_3,
  output [15:0] S,
  output C
);

  wire [15:0] xor_1_out;

  // Probe on in_1
  // Probe on in_2
  xor xor_1 (xor_1_out[0], in_2[0], in_3);
  xor xor_2 (xor_1_out[1], in_2[1], in_3);
  xor xor_3 (xor_1_out[2], in_2[2], in_3);
  xor xor_4 (xor_1_out[3], in_2[3], in_3);
  xor xor_5 (xor_1_out[4], in_2[4], in_3);
  xor xor_6 (xor_1_out[5], in_2[5], in_3);
  xor xor_7 (xor_1_out[6], in_2[6], in_3);
  xor xor_8 (xor_1_out[7], in_2[7], in_3);
  xor xor_9 (xor_1_out[8], in_2[8], in_3);
  xor xor_10 (xor_1_out[9], in_2[9], in_3);
  xor xor_11 (xor_1_out[10], in_2[10], in_3);
  xor xor_12 (xor_1_out[11], in_2[11], in_3);
  xor xor_13 (xor_1_out[12], in_2[12], in_3);
  xor xor_14 (xor_1_out[13], in_2[13], in_3);
  xor xor_15 (xor_1_out[14], in_2[14], in_3);
  xor xor_16 (xor_1_out[15], in_2[15], in_3);
  L_16_bit_ADD l_16_bit_add_1 (.A(in_1), .B(xor_1_out), .in_3(in_3), .S(S), .C(C));  // open: Gm, Pm
  // Probe on S
endmodule

module four_bit_paralled_adder (
  input  [3:0] A,
  input  [3:0] B,
  input  Cin,
  output [3:0] S,
  output Pm,
  output Gm,
  output C
);

  wire and_1_out, and_2_out, and_3_out, and_4_out, four_bit_parallel_carry_1_c1,
       four_bit_parallel_carry_1_c2, four_bit_parallel_carry_1_c3, or_1_out, or_2_out, or_3_out, or_4_out;

  and and_1 (and_1_out, A[0], B[0]);
  and and_2 (and_2_out, A[1], B[1]);
  and and_3 (and_3_out, A[2], B[2]);
  and and_4 (and_4_out, A[3], B[3]);
  or or_1 (or_1_out, A[0], B[0]);
  or or_2 (or_2_out, A[1], B[1]);
  or or_3 (or_3_out, A[2], B[2]);
  or or_4 (or_4_out, A[3], B[3]);
  four_bit_parallel_carry four_bit_parallel_carry_1 (
    .G0(and_1_out), .P0(or_1_out), .G1(and_2_out), .P1(or_2_out), .G2(and_3_out), .P2(or_3_out),
    .G3(and_4_out), .P3(or_4_out), .Cin(Cin), .C1(four_bit_parallel_carry_1_c1),
    .C2(four_bit_parallel_carry_1_c2), .C3(four_bit_parallel_carry_1_c3), .C4(C), .Gm(Gm), .Pm(Pm));
  full_adder full_adder_1 (.A(B[0]), .B(A[0]), .So(S[0]));  // open: C, Co
  full_adder full_adder_2 (.C(four_bit_parallel_carry_1_c1), .A(B[1]), .B(A[1]), .So(S[1]));  // open: Co
  full_adder full_adder_3 (.C(four_bit_parallel_carry_1_c2), .A(B[2]), .B(A[2]), .So(S[2]));  // open: Co
  full_adder full_adder_4 (.C(B[3]), .A(four_bit_parallel_carry_1_c3), .B(A[3]), .So(S[3]));  // open: Co
endmodule

module four_bit_parallel_adder_test (
  input  in_1
);

  wire clock_1_out;
  wire [3:0] counter_1_q, counter_1_q_2, four_bit_paralled_adder_1_s;
  wire [4:4] four_bit_paralled_adder_1_c;

  Counter counter_1 (
    .Q({counter_1_q_2, counter_1_q}), .up(1'b1), .clk(clock_1_out), .clr(in_1));  // open: load, D, count, carry
  // Probe on {counter_1_q_2, counter_1_q}
  Clock clock_1 (.out(clock_1_out));
  four_bit_paralled_adder four_bit_paralled_adder_1 (
    .A(counter_1_q_2), .B(counter_1_q), .S(four_bit_paralled_adder_1_s), .C(four_bit_paralled_adder_1_c[4]));  // open: Cin, Pm, Gm
  RAM #(.dataWidth(5)) ram_1 (
    .addr({counter_1_q_2, counter_1_q}), .we(1'b1), .clk(clock_1_out),
    .din({four_bit_paralled_adder_1_c[4], four_bit_paralled_adder_1_s}));  // open: oe, dout
  // Probe on {four_bit_paralled_adder_1_c[4], four_bit_paralled_adder_1_s}
  // Probe on {four_bit_paralled_adder_1_c[4], four_bit_paralled_adder_1_s}
endmodule

module four_bit_parallel_carry (
  input  G0,
  input  P0,
  input  G1,
  input  P1,
  input  G2,
  input  P2,
  input  G3,
  input  P3,
  input  Cin,
  output C1,
  output C2,
  output C3,
  output C4,
  output Gm,
  output Pm
);

  wire and_1_out, and_2_out, and_3_out, and_4_out, and_5_out, and_6_out, and_7_out, and_8_out, and_9_out,
       and_10_out, and_11_out, and_12_out, and_13_out;

  and and_1 (and_1_out, P0, Cin);
  and and_2 (and_2_out, P1, G0);
  and and_3 (and_3_out, P1, P0, Cin);
  and and_4 (and_4_out, P2, G1);
  and and_5 (and_5_out, P2, P1, G0);
  and and_6 (and_6_out, P2, P1, P0, Cin);
  and and_7 (and_7_out, P3, G2);
  and and_8 (and_8_out, P3, P2, G1);
  and and_9 (and_9_out, P3, P2, P1, G0);
  and and_10 (and_10_out, P3, P2, P1, P0, Cin);
  and and_11 (and_11_out, P3, G2);
  and and_12 (and_12_out, P3, P2, G1);
  and and_13 (and_13_out, P3, P2, P1, G0);
  and and_14 (Pm, P3, P2, P1, P0);
  or or_1 (C1, G0, and_1_out);
  or or_2 (C2, G1, and_2_out, and_3_out);
  or or_3 (C3, G2, and_4_out, and_5_out, and_6_out);
  or or_4 (C4, G3, and_7_out, and_8_out, and_9_out, and_10_out);
  or or_5 (Gm, G3, and_11_out, and_12_out, and_13_out);
endmodule

module four_bit_adder (
  input  [3:0] A,
  input  [3:0] B,
  output [3:0] Si,
  output Ci
);

  wire full_adder_1_co, full_adder_2_co, full_adder_3_co;

  // Probe on A
  // Probe on B
  full_adder full_adder_1 (.A(A[0]), .B(B[0]), .So(Si[0]), .Co(full_adder_1_co));  // open: C
  full_adder full_adder_2 (.C(full_adder_1_co), .A(A[1]), .B(B[1]), .So(Si[1]), .Co(full_adder_2_co));
  full_adder full_adder_3 (.C(full_adder_2_co), .A(A[2]), .B(B[2]), .So(Si[2]), .Co(full_adder_3_co));
  full_adder full_adder_4 (.C(full_adder_3_co), .A(A[3]), .B(B[3]), .So(Si[3]), .Co(Ci));
endmodule

module full_adder (
  input  C,
  input  A,
  input  B,
  output So,
  output Co
);

  wire and_1_out, and_2_out, xor_1_out;

  xor xor_1 (xor_1_out, A, B);
  and and_1 (and_1_out, A, B);
  and and_2 (and_2_out, C, xor_1_out);
  xor xor_2 (So, C, xor_1_out);
  or or_1 (Co, and_2_out, and_1_out);
endmodule
